# Fritzing sketch project (saved by Fritzing 0.9.4)

parts:
  Part1 = Arduino Uno (Rev3)
  Part2 = LCD1602-I2C
  Keypad4x1 = Keypad Membran 4x4
  A1 = 2 channel relay module [package=THT]
  BAT1 = Battery Holders [package=battery-aa]
  M2 = DC Motor
  M3 = DC Motor
  Load_Cell1 = Load Cell - Red/white/black/green
  Part3 = HX711 Weighing Sensor Module

nets:
  N1: Part1.A0, Part3.CK/TX
  N2: Part1.A1, Part3.DO/RX
  N3: Part1.D8, Keypad4x1.Pin7
  N4: Part1.D9_PWM, Keypad4x1.Pin8
  N5: Part1.D10_PWM/SS, A1.pin_15
  N6: Part1.D11_PWM/MOSI, A1.pin_16
  N7: Part1.A4/SDA, Part2.SDA
  N8: Part1.A5/SCL, Part2.SCL
  N9: Part1.D2, Keypad4x1.Pin1
  N10: Part1.D3_PWM, Keypad4x1.Pin2
  N11: Part1.D4, Keypad4x1.Pin3
  N12: Part1.D5_PWM, Keypad4x1.Pin4
  N13: Part1.D6_PWM, Keypad4x1.Pin5
  N14: Part1.D7, Keypad4x1.Pin6
  VCC: Part1.5V, Part2.VCC, A1.pin_13, Part3.VCC
  GND: Part1.GND, Part2.GND, A1.pin_14, Part3.GND
  N15: A1.pin_3, M2.pin_1
  N16: A1.pin_5, BAT1.+
  N17: A1.pin_6, M3.pin_1
  N18: BAT1.-, M3.pin_2
  N19: Load_Cell1.wire1, Part3.A+
  N20: Load_Cell1.wire2, Part3.A-
  N21: Load_Cell1.wire3, Part3.B+
  N22: Load_Cell1.wire4, Part3.B-

custom parts:
  LCD1602-I2C: A standard character display, usually with 2x16 characters. Comes in many colors with LCM1602 IIC attached.
  Keypad Membran 4x4: Membrane Keypad 4x4 Matrix
  2 channel relay module: 2 channel Relay Module 5V 12V 24V High and Low Level Trigger Relay Control With Optocoupler Two Way relays DC 5 V 12 V 24 V Volt.
  Load Cell - Red/white/black/green: A rectangle load cell/weighting pressure Sensor with four wires - Red, white, black, green. Normally corresponding with E+, E-, A+, A- respectively.
  HX711 Weighing Sensor Module: HX711 is a precision 24-bit analog-to-digital converter (ADC) designed for weigh scales and industrial control applications to interface directly with a bridge sensor.
